// Logisim project alu.circ as structural Verilog: 6 circuits, main circuit main
module main (
  input  [15:0] X,
  input  [15:0] Y,
  input  [3:0] Switch__S,
  output Signed_Overflow,
  output [15:0] RESULT,
  output Equal
);

  wire comparator_1_eq, comparator_2_eq, comparator_3_lt, of2, of3, overflow_1_out, ovf2, ovf3;
  wire [3:0] ys;
  wire [15:0] add, addp8, \and , \or , sllv, slt, srav, srlv, sub, subp8;

  BitSelector #(.width(16), .group(4)) bitselector_1 (.in(Y), .out(ys), .sel(2'b00));
  Comparator #(.width(4), .mode("unsigned")) comparator_1 (
    .a(Switch__S), .b(4'b1000), .eq(comparator_1_eq));  // open: gt, lt
  and and_1 (ovf2, of2, comparator_1_eq);
  Adder #(.width(16)) adder_1 (.a(X), .b(Y), .out(add));  // open: cin, cout
  addp8 addp8_1 (.X(X), .Y(Y), .result(addp8), .overflow(of2));
  Multiplexer #(.select(4), .width(16)) multiplexer_1 (
    .in0(add), .in1(sub), .in2(sllv), .in3(srlv), .in4(srav), .in5(slt), .in6(\or ), .in7(\and ),
    .in8(addp8), .in9(subp8), .out(RESULT), .sel(Switch__S));  // open: in10, in11, in12, in13, in14, in15, en
  Comparator #(.width(4), .mode("unsigned")) comparator_2 (
    .a(Switch__S), .b(4'b1001), .eq(comparator_2_eq));  // open: gt, lt
  Subtractor #(.width(16)) subtractor_1 (.a(X), .b(Y), .out(sub));  // open: bin, bout
  subp8 subp8_1 (.X(X), .Y(Y), .result(subp8), .overflow(of3));
  and and_2 (ovf3, of3, comparator_2_eq);
  Shifter #(.width(16)) shifter_1 (.in(X), .\dist (ys), .out(sllv));
  Comparator #(.width(16)) comparator_3 (.a(X), .b(Y), .eq(Equal), .lt(comparator_3_lt));  // open: gt
  assign \or  = X | Y;  // OR_Gate or_1, 16 bits wide
  overflow overflow_1 (.y(Y), .x(X), .plus(add), .sub(sub), .out(overflow_1_out), .s(Switch__S));
  Shifter #(.width(16), .shift("lr")) shifter_2 (.in(X), .\dist (ys), .out(srlv));
  assign slt = {{15{1'b0}}, comparator_3_lt};  // Bit_Extender bit_extender_1
  or or_2 (Signed_Overflow, overflow_1_out, ovf2, ovf3);
  assign \and  = X & Y;  // AND_Gate and_3, 16 bits wide
  Shifter #(.width(16), .shift("ar")) shifter_3 (.in(X), .\dist (ys), .out(srav));

  // Other names for the same wires on the sheet: eq = Equal; of = Signed_Overflow; res[15:0] = RESULT;
  //   s[3:0] = Switch__S

  // Notes on the sheet:
  //   INPUTS to your circuit
  //   INPUT to your circuit
  //   DON'T CHANGE THE INPUTS AND OUTPUTS! IF YOU DO SO, YOU NEED TO MAKE SURE THE PINS ARE IN THE RIGHT PLACES!
  //   OUTPUTS of your circuit
endmodule

module addp8 (
  input  [15:0] X,
  input  [15:0] Y,
  output [15:0] result,
  output overflow
);

  wire ov0, ov1;

  Adder adder_1 (.a(X[7:0]), .b(Y[7:0]), .out(result[7:0]));  // open: cin, cout
  Adder adder_2 (.a(X[15:8]), .b(Y[15:8]), .out(result[15:8]));  // open: cin, cout
  overflow_ap8 overflow_ap8_1 (.y(Y[7:0]), .x(X[7:0]), .plus(result[7:0]), .out(ov0));
  overflow_ap8 overflow_ap8_2 (.y(Y[15:8]), .x(X[15:8]), .plus(result[15:8]), .out(ov1));
  or or_1 (overflow, ov0, ov1);

  // Other names for the same wires on the sheet: x0[7:0] = X[7:0]; x1[7:0] = X[15:8]; y0[7:0] = Y[7:0];
  //   y1[7:0] = Y[15:8]
endmodule

module subp8 (
  input  [15:0] X,
  input  [15:0] Y,
  output [15:0] result,
  output overflow
);

  wire ov0, ov1;

  Subtractor subtractor_1 (.a(X[7:0]), .b(Y[7:0]), .out(result[7:0]));  // open: bin, bout
  Subtractor subtractor_2 (.a(X[15:8]), .b(Y[15:8]), .out(result[15:8]));  // open: bin, bout
  overflow_sp8 overflow_sp8_1 (.y(Y[7:0]), .x(X[7:0]), .sub(result[7:0]), .out(ov0));
  overflow_sp8 overflow_sp8_2 (.y(Y[15:8]), .x(X[15:8]), .sub(result[15:8]), .out(ov1));
  or or_1 (overflow, ov0, ov1);

  // Other names for the same wires on the sheet: x0[7:0] = X[7:0]; x1[7:0] = X[15:8]; y0[7:0] = Y[7:0];
  //   y1[7:0] = Y[15:8]
endmodule

module overflow (
  input  [15:0] y,
  input  [15:0] x,
  input  [15:0] plus,
  input  [15:0] sub,
  input  [3:0] s,
  output out
);

  wire and_1_out, and_2_out, and_3_out, and_4_out, and_5_out, and_6_out, comparator_1_eq, comparator_2_eq,
       nm, or_1_out, or_2_out, pm, xm, ym;

  BitSelector #(.width(16)) bitselector_1 (.in(y), .out(ym), .sel(4'b1111));
  BitSelector #(.width(16)) bitselector_2 (.in(x), .out(xm), .sel(4'b1111));
  BitSelector #(.width(16)) bitselector_3 (.in(plus), .out(pm), .sel(4'b1111));
  BitSelector #(.width(16)) bitselector_4 (.in(sub), .out(nm), .sel(4'b1111));
  and and_1 (and_1_out, ~xm, ~ym, pm);  // AND_Gate
  and and_2 (and_2_out, xm, ym, ~pm);  // AND_Gate
  and and_3 (and_3_out, xm, ~ym, ~nm);  // AND_Gate
  and and_4 (and_4_out, ~xm, ym, nm);  // AND_Gate
  or or_1 (or_1_out, and_1_out, and_2_out);
  Comparator #(.width(4)) comparator_1 (.a(s), .b(4'b0000), .eq(comparator_1_eq));  // open: gt, lt
  or or_2 (or_2_out, and_3_out, and_4_out);
  Comparator #(.width(4)) comparator_2 (.a(s), .b(4'b0001), .eq(comparator_2_eq));  // open: gt, lt
  and and_5 (and_5_out, or_1_out, comparator_1_eq);
  and and_6 (and_6_out, or_2_out, comparator_2_eq);
  or or_3 (out, and_5_out, and_6_out);
endmodule

module overflow_ap8 (
  input  [7:0] y,
  input  [7:0] x,
  input  [7:0] plus,
  output out
);

  wire and_1_out, and_2_out, pm, xm, ym;

  BitSelector bitselector_1 (.in(y), .out(ym), .sel(3'b111));
  BitSelector bitselector_2 (.in(x), .out(xm), .sel(3'b111));
  BitSelector bitselector_3 (.in(plus), .out(pm), .sel(3'b111));
  and and_1 (and_1_out, ~xm, ~ym, pm);  // AND_Gate
  and and_2 (and_2_out, xm, ym, ~pm);  // AND_Gate
  or or_1 (out, and_1_out, and_2_out);
endmodule

module overflow_sp8 (
  input  [7:0] y,
  input  [7:0] x,
  input  [7:0] sub,
  output out
);

  wire and_1_out, and_2_out, nm, xm, ym;

  BitSelector bitselector_1 (.in(y), .out(ym), .sel(3'b111));
  BitSelector bitselector_2 (.in(x), .out(xm), .sel(3'b111));
  BitSelector bitselector_3 (.in(sub), .out(nm), .sel(3'b111));
  and and_1 (and_1_out, xm, ~ym, ~nm);  // AND_Gate
  and and_2 (and_2_out, ~xm, ym, nm);  // AND_Gate
  or or_1 (out, and_1_out, and_2_out);
endmodule
