// Logisim project Regfile.circ as structural Verilog: 2 circuits, main circuit main
module main (
  input  [1:0] Read_register_1,
  input  [1:0] Read_register_2,
  input  [1:0] write_register,
  input  [15:0] write_data,
  input  RegWrite,
  input  clock,
  output [15:0] Reg_0_Value,
  output [15:0] Reg_1_Value,
  output [15:0] Reg_2_Value,
  output [15:0] Reg_3_Value,
  output [15:0] Read_Data_1,
  output [15:0] Read_Data_2
);

  wire [15:0] in0, in1, in2, in3;

  Register #(.width(16)) r0 (.D(in0), .Q(Reg_0_Value), .clk(clock));  // open: en, clr
  Register #(.width(16)) r1 (.D(in1), .Q(Reg_1_Value), .clk(clock));  // open: en, clr
  Register #(.width(16)) r2 (.D(in2), .Q(Reg_2_Value), .clk(clock));  // open: en, clr
  writeControl writecontrol_1 (
    .out0(Reg_0_Value), .out1(Reg_1_Value), .write_bits(write_data), .out2(Reg_2_Value), .out3(Reg_3_Value),
    .regw(RegWrite), .reg_sel(write_register), .in0(in0), .in1(in1), .in2(in2), .in3(in3));
  Register #(.width(16)) r3 (.D(in3), .Q(Reg_3_Value), .clk(clock));  // open: en, clr
  Multiplexer #(.select(2), .width(16)) multiplexer_1 (
    .in0(Reg_0_Value), .in1(Reg_1_Value), .in2(Reg_2_Value), .in3(Reg_3_Value), .out(Read_Data_1),
    .sel(Read_register_1));  // open: en
  Multiplexer #(.select(2), .width(16)) multiplexer_2 (
    .in0(Reg_0_Value), .in1(Reg_1_Value), .in2(Reg_2_Value), .in3(Reg_3_Value), .out(Read_Data_2),
    .sel(Read_register_2));  // open: en

  // Other names for the same wires on the sheet: clk = clock; dat[15:0] = write_data; out0[15:0] = Reg_0_Value;
  //   out1[15:0] = Reg_1_Value; out2[15:0] = Reg_2_Value; out3[15:0] = Reg_3_Value; read1[1:0] = Read_register_1;
  //   read2[1:0] = Read_register_2; regw = RegWrite; wr_reg[1:0] = write_register

  // Notes on the sheet:
  //   These are INPUTS to the circuit
  //   These are INPUTS to the circuit
  //   DO NOT CHANGE THE LOCATIONS OF THE INPUTS/OUTPUTS! IF YOU DO SO, YOU NEED TO MAKE SURE THE PINS ARE AT THE RIGHT PLACE!
  //   These are OUTPUTS to the circuit
  //   write control
  //   Yet again, the clock is not an actual clock, but an input, one that will be driven from a higher circuit
  //   These are OUTPUTS to the circuit
endmodule

module writeControl (
  input  [15:0] out0,
  input  [15:0] out1,
  input  [15:0] write_bits,
  input  [15:0] out2,
  input  [15:0] out3,
  input  regw,
  input  [1:0] reg_sel,
  output [15:0] in0,
  output [15:0] in1,
  output [15:0] in2,
  output [15:0] in3
);

  wire comparator_1_eq, comparator_2_eq, comparator_3_eq, comparator_4_eq, s0, s1, s2, s3;
  wire [15:0] demultiplexer_1_out0, demultiplexer_1_out1, demultiplexer_1_out2, demultiplexer_1_out3;

  Demultiplexer #(.select(2), .width(16)) demultiplexer_1 (
    .out0(demultiplexer_1_out0), .out1(demultiplexer_1_out1), .out2(demultiplexer_1_out2),
    .out3(demultiplexer_1_out3), .in(write_bits), .sel(reg_sel));  // open: en
  Comparator #(.width(2)) comparator_1 (.a(reg_sel), .b(2'b00), .eq(comparator_1_eq));  // open: gt, lt
  Comparator #(.width(2)) comparator_2 (.a(reg_sel), .b(2'b01), .eq(comparator_2_eq));  // open: gt, lt
  and and_1 (s0, comparator_1_eq, regw);
  and and_2 (s1, comparator_2_eq, regw);
  Multiplexer #(.width(16)) multiplexer_1 (.in0(out0), .in1(demultiplexer_1_out0), .out(in0), .sel(s0));  // open: en
  Multiplexer #(.width(16)) multiplexer_2 (.in0(out1), .in1(demultiplexer_1_out1), .out(in1), .sel(s1));  // open: en
  Multiplexer #(.width(16)) multiplexer_3 (.in0(out2), .in1(demultiplexer_1_out2), .out(in2), .sel(s2));  // open: en
  Multiplexer #(.width(16)) multiplexer_4 (.in0(out3), .in1(demultiplexer_1_out3), .out(in3), .sel(s3));  // open: en
  Comparator #(.width(2)) comparator_3 (.a(reg_sel), .b(2'b10), .eq(comparator_3_eq));  // open: gt, lt
  Comparator #(.width(2)) comparator_4 (.a(reg_sel), .b(2'b11), .eq(comparator_4_eq));  // open: gt, lt
  and and_3 (s2, comparator_3_eq, regw);
  and and_4 (s3, comparator_4_eq, regw);

  // Other names for the same wires on the sheet: regwr = regw; select[1:0] = reg_sel
endmodule
