// Logisim project cpu.circ as structural Verilog: 2 circuits, main circuit main
module main (
  input  reset,
  input  [15:0] From_Instr_Mem,
  input  clk,
  output [15:0] r0,
  output [15:0] r1,
  output [15:0] r2,
  output [15:0] r3,
  output [15:0] Display_0,
  output [15:0] Display_1,
  output [15:0] Data_Mem_Data,
  output [15:0] To_Instr_Mem,
  output Data_Mem_Write,
  output [15:0] Data_Mem_Addr
);

  wire ALU_eq, ALU_src, and_2_out, and_3_out, and_5_out, and_7_out, branch, disp, kill, not_1_out, o0, o1,
       o2, o3, o4, o5, o6, o7, o8, o10, o11, o12, or_7_out, or_8_out, ovf, REG_dst, REG_write;
  wire [1:0] ALU_to_REG, and_4_out, and_6_out, bit_extender_2_out, bit_extender_3_out, bit_extender_4_out,
       bit_extender_5_out, bit_extender_6_out, bit_extender_7_out, bit_extender_8_out, multiplexer_4_out,
       multiplexer_6_out, nPC_sel;
  wire [3:0] ALU_ctr, bitselector_2_out, multiplexer_8_out, multiplexer_10_out, multiplexer_12_out, opcode;
  wire [5:0] funct;
  wire [11:6] inst;
  wire [15:0] adder_1_out, and_1_out, bit_extender_1_out, data_out, di0, di1, immi_off, j_addr, lui_res,
       multiplexer_1_out, multiplexer_2_out, multiplexer_5_out, multiplexer_7_out, multiplexer_9_out,
       multiplexer_11_out, nextPC, R_rs, target;

  or or_1 (REG_dst, o1, o0);
  Decoder #(.select(4), .enable("false")) decoder_1 (
    .out0(o0), .out1(o1), .out2(o2), .out3(o3), .out4(o4), .out5(o5), .out6(o6), .out7(o7), .out8(o8),
    .out9(Data_Mem_Write), .out10(o10), .out11(o11), .out12(o12), .sel(opcode));  // open: out13, out14, out15
  not not_1 (not_1_out, Data_Mem_Write);
  assign and_1_out = To_Instr_Mem & 16'hf000;  // AND_Gate and_1, 16 bits wide
  Multiplexer #(.width(16)) multiplexer_1 (
    .in0(immi_off), .in1(Data_Mem_Data), .out(multiplexer_1_out), .sel(ALU_src));  // open: en
  or or_2 (ALU_src, o0, o8, o4);
  assign data_out = Data_Mem_Write ? Data_Mem_Data : 16'bz;  // Controlled_Buffer controlled_buffer_1
  RAM #(.addrWidth(16), .dataWidth(16)) ram_1 (
    .addr(Data_Mem_Addr), .data(data_out), .sel(1'b1), .clk(clk), .ld(not_1_out), .clr(reset));
  Multiplexer #(.width(16)) multiplexer_2 (
    .in0(From_Instr_Mem), .in1(16'h6), .out(multiplexer_2_out), .sel(kill));  // open: en
  assign bit_extender_1_out = {{4{1'b0}}, {inst, funct}};  // Bit_Extender bit_extender_1
  alu_main main_1 (
    .Switch__S(ALU_ctr), .X(R_rs), .Equal(ALU_eq), .RESULT(Data_Mem_Addr), .Signed_Overflow(ovf),
    .Y(multiplexer_1_out));
  and and_2 (and_2_out, o8, ~ALU_eq);  // AND_Gate
  and and_3 (and_3_out, o4, ALU_eq);
  Register #(.width(16)) register_1 (.D(multiplexer_2_out), .Q({opcode, inst, funct}), .clk(clk));  // open: en, clr
  extend extend_1 (.obj({inst[7:6], funct}), .opcode(opcode), .out_3(immi_off));
  assign j_addr = bit_extender_1_out | and_1_out;  // OR_Gate or_3, 16 bits wide
  or or_4 (REG_write, o0, o1, o5, o6, o7, o10, o11);
  Adder #(.width(16)) adder_1 (.a(To_Instr_Mem), .b(immi_off), .out(adder_1_out));  // open: cin, cout
  or or_5 (branch, and_2_out, and_3_out);
  BitSelector #(.width(16)) bitselector_1 (.in(immi_off), .out(disp), .sel(4'b0000));
  assign bit_extender_2_out = {{1{o1}}, o1};  // Bit_Extender bit_extender_2
  assign bit_extender_3_out = {{1{1'b0}}, o11};  // Bit_Extender bit_extender_3
  assign bit_extender_4_out = {{1{o10}}, o10};  // Bit_Extender bit_extender_4
  Multiplexer #(.width(16)) multiplexer_3 (.in0(nextPC), .in1(adder_1_out), .out(target), .sel(branch));  // open: en
  Demultiplexer #(.select(2), .width(16), .enable("false")) demultiplexer_1 (
    .out2(di0), .out3(di1), .in(R_rs), .sel(bit_extender_5_out));  // open: out0, out1
  assign bit_extender_5_out = {{1{1'b1}}, disp};  // Bit_Extender bit_extender_5
  LED led_1 (.in(ovf));
  Hex_Digit_Display hex_digit_display_1 (.value(Display_0[15:12]));  // open: dp
  Multiplexer #(.width(2)) multiplexer_4 (.in0(inst[7:6]), .in1(2'b11), .out(multiplexer_4_out), .sel(o1));  // open: en
  assign ALU_to_REG = bit_extender_2_out | bit_extender_3_out | and_4_out;  // OR_Gate or_6, 2 bits wide
  assign and_4_out = bit_extender_4_out & 2'b10;  // AND_Gate and_4, 2 bits wide
  Hex_Digit_Display hex_digit_display_2 (.value(Display_0[7:4]));  // open: dp
  Hex_Digit_Display hex_digit_display_3 (.value(Display_0[11:8]));  // open: dp
  Multiplexer #(.width(16)) multiplexer_5 (
    .in0(Display_0), .in1(di0), .out(multiplexer_5_out), .sel(and_5_out));  // open: en
  Register #(.width(16)) register_2 (.D(multiplexer_5_out), .Q(Display_0), .clk(clk));  // open: en, clr
  and and_5 (and_5_out, ~disp, o12);  // AND_Gate
  Adder #(.width(16)) adder_2 (.a(To_Instr_Mem), .b(16'h1), .out(nextPC));  // open: cin, cout
  Hex_Digit_Display hex_digit_display_4 (.value(Display_0[3:0]));  // open: dp
  Multiplexer #(.width(2)) multiplexer_6 (
    .in0(inst[9:8]), .in1(multiplexer_4_out), .out(multiplexer_6_out), .sel(REG_dst));  // open: en
  Multiplexer #(.select(2), .width(16)) multiplexer_7 (
    .in0(Data_Mem_Addr), .in1(data_out), .in2(lui_res), .in3(To_Instr_Mem), .out(multiplexer_7_out),
    .sel(ALU_to_REG));  // open: en
  Multiplexer #(.width(4)) multiplexer_8 (.in0(4'b0000), .in1(4'b0111), .out(multiplexer_8_out), .sel(o6));  // open: en
  or or_7 (or_7_out, o1, o2);
  assign bit_extender_6_out = {{1{o3}}, o3};  // Bit_Extender bit_extender_6
  or or_8 (or_8_out, o8, o4);
  Hex_Digit_Display hex_digit_display_5 (.value(Display_1[11:8]));  // open: dp
  Hex_Digit_Display hex_digit_display_6 (.value(Display_1[15:12]));  // open: dp
  Multiplexer #(.select(2), .width(16)) multiplexer_9 (
    .in0(nextPC), .in1(target), .in2(j_addr), .in3(R_rs), .out(multiplexer_9_out), .sel(nPC_sel));  // open: en
  Multiplexer #(.width(4)) multiplexer_10 (
    .in0(4'b0000), .in1(4'b0110), .out(multiplexer_10_out), .sel(o7));  // open: en
  BitSelector #(.width(6), .group(4)) bitselector_2 (.in(funct), .out(bitselector_2_out), .sel(1'b0));
  assign bit_extender_7_out = {{1{or_7_out}}, or_7_out};  // Bit_Extender bit_extender_7
  assign and_6_out = bit_extender_7_out & 2'b10;  // AND_Gate and_6, 2 bits wide
  assign bit_extender_8_out = {{1{1'b0}}, or_8_out};  // Bit_Extender bit_extender_8
  Hex_Digit_Display hex_digit_display_7 (.value(Display_1[7:4]));  // open: dp
  Hex_Digit_Display hex_digit_display_8 (.value(Display_1[3:0]));  // open: dp
  Multiplexer #(.width(16)) multiplexer_11 (
    .in0(Display_1), .in1(di1), .out(multiplexer_11_out), .sel(and_7_out));  // open: en
  and and_7 (and_7_out, disp, o12);
  Register #(.width(16)) PC (.D(multiplexer_9_out), .Q(To_Instr_Mem), .clk(clk));  // open: en, clr
  Regfile_main main_2 (
    .Read_register_1(inst[11:10]), .Read_register_2(inst[9:8]), .write_register(multiplexer_6_out),
    .write_data(multiplexer_7_out), .Reg_0_Value(r0), .Reg_1_Value(r1), .Reg_2_Value(r2), .Reg_3_Value(r3),
    .RegWrite(REG_write), .clock(clk), .Read_Data_1(R_rs), .Read_Data_2(Data_Mem_Data));
  Multiplexer #(.width(4)) multiplexer_12 (
    .in0(4'b0000), .in1(bitselector_2_out), .out(multiplexer_12_out), .sel(o0));  // open: en
  or or_9 (kill, branch, o1, o2, o3);
  Shifter #(.width(16)) shifter_1 (.in(immi_off), .\dist (4'b1000), .out(lui_res));
  assign nPC_sel = and_6_out | bit_extender_6_out | bit_extender_8_out;  // OR_Gate or_10, 2 bits wide
  Register #(.width(16)) register_3 (.D(multiplexer_11_out), .Q(Display_1), .clk(clk));  // open: en, clr
  assign ALU_ctr = multiplexer_8_out | multiplexer_10_out | multiplexer_12_out;  // OR_Gate or_11, 4 bits wide

  // Other names for the same wires on the sheet: inst[5:0] = funct; rd[1:0] = inst[7:6]; rt[1:0] = inst[9:8];
  //   rs[1:0] = inst[11:10]; ck = clk; curPC[15:0] = To_Instr_Mem; d0[15:0] = Display_0; d1[15:0] = Display_1;
  //   ALU_res[15:0] = Data_Mem_Addr; data_ad[15:0] = Data_Mem_Addr; data_in[15:0] = Data_Mem_Data;
  //   R_rt[15:0] = Data_Mem_Data; MEM_write = Data_Mem_Write; o9 = Data_Mem_Write

  // Notes on the sheet:
  //   This is the current PC that you need to send as OUTPUT
  //   DATA MEMORY
  //   INPUTS/INSTRUCTION FETCH
  //   This is the instruction that you would receive as INPUT
  //   This is a CLK that is an INPUT driven from the harness.
  //   Remember, this circuit is loaded from the harness to be tested!
  //   INSTRUCTION DECODING
  //   ALU
  //   DO NOT CHANGE THE LOCATIONS OF THE INPUTS OR OUTPUTS! IF YOU DO SO, YOU NEED TO MAKE SURE THE PINS ARE IN THE RIGHT PLACES!
  //   CONTROL BLOCK
  //   These are OUTPUTS of the circuit
  //   DISPLAY
  //   OUTPUTS
  //   These are OUTPUTS of the circuit
  //   PROGRAM COUNTER
  //   REGISTER BLOCK
endmodule

module extend (
  input  [7:0] obj,
  input  [3:0] opcode,
  output [15:0] out_3
);

  wire comparator_1_eq, comparator_2_eq, comparator_3_eq, comparator_4_eq, comparator_5_eq, or_1_out;
  wire [15:0] bit_extender_1_out, bit_extender_2_out;

  assign bit_extender_1_out = {{8{1'b0}}, obj};  // Bit_Extender bit_extender_1
  assign bit_extender_2_out = {{8{obj[7]}}, obj};  // Bit_Extender bit_extender_2
  Comparator #(.width(4)) comparator_1 (.a(opcode), .b(4'b0100), .eq(comparator_1_eq));  // open: gt, lt
  Comparator #(.width(4)) comparator_2 (.a(opcode), .b(4'b0101), .eq(comparator_2_eq));  // open: gt, lt
  Comparator #(.width(4)) comparator_3 (.a(opcode), .b(4'b1000), .eq(comparator_3_eq));  // open: gt, lt
  Comparator #(.width(4)) comparator_4 (.a(opcode), .b(4'b1001), .eq(comparator_4_eq));  // open: gt, lt
  Comparator #(.width(4)) comparator_5 (.a(opcode), .b(4'b1011), .eq(comparator_5_eq));  // open: gt, lt
  or or_1 (or_1_out, comparator_1_eq, comparator_2_eq, comparator_3_eq, comparator_4_eq, comparator_5_eq);
  Multiplexer #(.width(16)) multiplexer_1 (
    .in0(bit_extender_1_out), .in1(bit_extender_2_out), .out(out_3), .sel(or_1_out));  // open: en
endmodule
